# Fritzing sketch BRobotShield (saved by Fritzing 0.9.3b)
circuit board: 6.88566cm x 5.36311cm
breadboards: 1

parts:
  A4988_1 = Pololu A4988 [package=SO16]
  A4988_2 = Pololu A4988 [package=SO16]
  MOT1 = male pin header, 4 pins [form="♂ (male)"]
  MOT2 = male pin header, 4 pins [form="♂ (male)"]
  GY2 = MPU-6050 Board GY-521 [form="♀ (female)" package=THT]
  U1 = ESP8266 WiFi Module [part_number=ESP8266]
  R6 = Resistor [tolerance=±5% resistance=1k package=THT]
  R7 = Resistor [tolerance=±5% resistance=4.7k package=THT]
  R8 = Resistor [tolerance=±5% resistance=4.7k package=THT]
  R10 = Resistor [tolerance=±5% resistance=10k package=THT]
  R9 = Resistor [tolerance=±5% resistance=10k package=THT]
  R12 = Resistor [tolerance=±5% resistance=10k package=THT]
  R3 = Resistor [tolerance=±5% resistance=470 package=THT]
  R5 = Resistor [tolerance=±5% resistance=2.2k package=THT]
  R4 = Resistor [tolerance=±5% resistance=1k package=THT]
  C3 = Electrolytic Capacitor [capacitance=10µF package="100 mil [THT, electrolytic]"]
  C4 = Electrolytic Capacitor [capacitance=10µF package="100 mil [THT, electrolytic]"]
  C1 = Tantalum Capacitor [capacitance=10µF voltage=20V package="100 mil [THT, tantalum]"]
  C2 = Tantalum Capacitor [capacitance=10µF package="100 mil [THT, tantalum]"]
  SERVO1 = male pin header, 3 pins [form="♂ (male)"]
  SERVO2 = male pin header, 3 pins [form="♂ (male)"]
  VR1 = Voltage Regulator [package=to220-adj]
  R2 = Resistor [tolerance=±5% resistance=22k package=THT]
  R1 = Resistor [tolerance=±5% resistance=33k package=THT]
  R11 = Resistor [tolerance=±5% resistance=10k package=THT]
  BRobot = Arduino Leonardo (Rev3b)

nets:
  N1: A4988_1.ENABLE, A4988_2.ENABLE, R6.Pin_1, BRobot.D4/A6
  5V: A4988_1.MS1, A4988_1.MS2, A4988_1.VDD, A4988_2.MS1, A4988_2.MS2, A4988_2.VDD, GY2.pin1, R6.Pin_0, R7.Pin_0, R8.Pin_0, SERVO1.pin2, SERVO2.pin2, BRobot.5V
  N2: A4988_1.MS3, A4988_2.MS3, R7.Pin_1, R8.Pin_1, BRobot.A4
  N3: A4988_1.RESET, A4988_1.SLEEP
  N4: A4988_1.STEP, BRobot.D7
  N5: A4988_1.DIR, BRobot.D8/A8
  GND: A4988_1.GND, A4988_2.GND, GY2.pin2, U1.GND, R5.Pin_0, C3.-, C4.-, C1.-, C2.-, SERVO1.pin1, SERVO2.pin1, VR1.ADJ, R2.Pin_0, BRobot.GND
  N6: A4988_1.1B, MOT1.pin1
  N7: A4988_1.1A, MOT1.pin2
  N8: A4988_1.2A, MOT1.pin3
  N9: A4988_1.2B, MOT1.pin4
  9V: A4988_1.VMOT, A4988_2.VMOT, C3.+, C4.+, C1.+, VR1.IN, R1.Pin_1, BRobot.VIN
  N10: A4988_2.RESET, A4988_2.SLEEP
  N11: A4988_2.STEP, BRobot.D12/A11
  N12: A4988_2.DIR, BRobot.D5_PWM
  N13: A4988_2.1B, MOT2.pin1
  N14: A4988_2.1A, MOT2.pin2
  N15: A4988_2.2A, MOT2.pin3
  N16: A4988_2.2B, MOT2.pin4
  N17: GY2.pin3, BRobot.D3_PWM/SCL
  N18: GY2.pin4, BRobot.D2/SDA
  N19: U1.RXD, R4.Pin_0
  3.3V: U1.VCC, R10.Pin_0, R9.Pin_0, R12.Pin_0, C2.+, VR1.OUT, R11.Pin_0
  N20: U1.GPIO_0, R10.Pin_1
  N21: U1.RST, R12.Pin_1
  N22: U1.GPIO_2, R11.Pin_1
  N23: U1.CH_PD, R9.Pin_1
  N24: U1.TXD, R3.Pin_0
  N25: R3.Pin_1, BRobot.D0/RX
  N26: R5.Pin_1, R4.Pin_1, BRobot.D1/TX
  N27: SERVO1.pin3, BRobot.D10_PWM/A10
  N28: SERVO2.pin3, BRobot.D6_PWM/A7
  N29: R2.Pin_1, R1.Pin_0, BRobot.A5

custom parts:
  MPU-6050 Board GY-521: Acelerometro y Giroscopio MPU-6050 Board GY-521
  ESP8266 WiFi Module: Generic WiFi Module based on the ESP8266 with onboard PCB antenna and UART communications
  Voltage Regulator: Voltage Regulator Standard LM317 adjustable voltage regulator. AOI (Adjust Output Input). Google 'LM317 Calculator' for easy to use app to get the two resistor values needed. 240/720 for 5V output. 240/390 for 3.3V output. Spark Fun Electronics SKU : COM-00527
